// Logisim project LOGISIM PROJECT.circ as structural Verilog: 3 circuits, main circuit main
module main (
);

  wire clock_1_out, controlunit_1_regwrite;
  wire [1:0] Instructionmemory_data_2, Instructionmemory_data_3, Instructionmemory_data_4,
       Instructionmemory_data_5;
  wire [2:0] controlunit_1_aluop, PC_q;
  wire [3:0] A_q, alu_1_result, B_q, C_q, D_q, Instructionmemory_data, multiplexer_1_out;

  Clock clock_1 (.out(clock_1_out));
  Counter #(.max('h7), .width(3)) PC (
    .clr(1'b0), .load(1'b1), .up(1'b1), .count(1'b0), .clk(clock_1_out), .Q(PC_q));  // open: D, carry
  ROM #(.addrWidth(3), .dataWidth(12)) Instructionmemory (
    .addr(PC_q),
    .data({Instructionmemory_data_5, Instructionmemory_data_4, Instructionmemory_data_3, Instructionmemory_data_2, Instructionmemory_data}));
  Multiplexer #(.select(2), .width(4)) multiplexer_1 (
    .in0(A_q), .in1(B_q), .in2(C_q), .in3(D_q), .out(multiplexer_1_out), .sel(Instructionmemory_data_4));
  Multiplexer #(.select(2), .width(4)) multiplexer_2 (
    .in0(A_q), .in2(C_q), .in3(D_q), .out(multiplexer_1_out), .sel(Instructionmemory_data_3));  // open: in1
  ALU alu_1 (.A(B_q), .B(multiplexer_1_out), .ALUop(controlunit_1_aluop), .RESULT(alu_1_result));
  ControlUnit controlunit_1 (
    .opcode(Instructionmemory_data), .Regwrite(controlunit_1_regwrite), .ALUop(controlunit_1_aluop));  // open: ALUsrc
  Register #(.width(4)) A (.en(controlunit_1_regwrite), .clk(clock_1_out), .Q(A_q), .clr(1'b0));  // open: D
  Register #(.width(4)) B (.D(alu_1_result), .en(controlunit_1_regwrite), .clk(clock_1_out), .Q(B_q), .clr(1'b0));
  Register #(.width(4)) C (.D(alu_1_result), .en(controlunit_1_regwrite), .clk(clock_1_out), .Q(C_q), .clr(1'b0));
  Register #(.width(4)) D (.D(alu_1_result), .en(controlunit_1_regwrite), .clk(clock_1_out), .Q(D_q), .clr(1'b0));

  // Notes on the sheet:
  //   contents of Instructionmemory (hex, n*v repeats v):
  //   518 328 270 2d1 1e2 273 d5 f6c
endmodule

module ALU (
  input  [3:0] A,
  input  [3:0] B,
  input  [2:0] ALUop,
  output [3:0] RESULT
);

  wire [3:0] adder_1_out, AGATE_out, multiplexer_1_out, NGATE_out, OGATE_out, subtractor_1_out, XGATE_out;

  assign AGATE_out = A & B;  // AND_Gate AGATE, 4 bits wide
  assign OGATE_out = A | B;  // OR_Gate OGATE, 4 bits wide
  Subtractor #(.width(4)) subtractor_1 (.a(A), .b(B), .out(subtractor_1_out));  // open: bin, bout
  Adder #(.width(4)) adder_1 (.a(A), .b(B), .out(adder_1_out));  // open: cin, cout
  assign XGATE_out = A ^ B;  // XOR_Gate XGATE, 4 bits wide
  assign NGATE_out = ~A;  // NOT_Gate NGATE, 4 bits wide
  Multiplexer #(.select(3), .width(4)) multiplexer_1 (
    .in0(adder_1_out), .in1(subtractor_1_out), .in2(AGATE_out), .in3(OGATE_out), .in4(XGATE_out),
    .in5(NGATE_out), .out(multiplexer_1_out), .sel(ALUop));  // open: in6, in7
endmodule

module ControlUnit (
  input  [3:0] opcode,
  output Regwrite,
  output ALUsrc,
  output [2:0] ALUop
);

  ROM #(.addrWidth(4), .dataWidth(5)) ControlROM (.addr(opcode), .data({Regwrite, ALUsrc, ALUop}));

  // Notes on the sheet:
  //   contents of ControlROM (hex, n*v repeats v):
  //   10 11 12 13 14 15 0 0 18 0 1a 1b 1c
endmodule
